# Fritzing sketch netduino sensor (saved by Fritzing 0.9.3b)

parts:
  Netduino1 = Netduino
  Grove1 = Grove Light Sensor
  Componente3 = FTDI Basic Programmer
  Grove2 = Grove Temperature Sensor

nets:
  GND: Netduino1.GND, Grove1.GND, Componente3.GND, Grove2.GND
  N1: Netduino1.D1_TX0, Componente3.RXI
  N2: Netduino1.D0_RX0, Componente3.TXO
  VCC: Netduino1.3V3, Grove1.VCC, Grove2.VCC
  N3: Netduino1.A0, Grove2.SIG
  N4: Netduino1.A1, Grove1.SIG
